# Fritzing sketch pi_fllod_detector (saved by Fritzing 0.8.0b)

parts:
  Raspberry_Pi1 = Raspberry Pi
  R1 = Resistor [tolerance=±5% resistance=1M package="0805 [SMD]"]
  R2 = Resistor [tolerance=±5% resistance=1M package="0805 [SMD]"]
  R3 = Resistor [tolerance=±5% resistance=1M package="0805 [SMD]"]
  J1 = female pin header, 5 pins [form="♀ (female)"]
  J2 = female pin header, 2 pins [form="♀ (female)"]
  J3 = female pin header, 2 pins [form="♀ (female)"]
  J4 = female pin header, 2 pins [form="♀ (female)"]
  R2_2 = Resistor [tolerance=±5% resistance=1M package=THT]
  R3_2 = Resistor [tolerance=±5% resistance=1M package=THT]
  J4_2 = female pin header, 5 pins [form="♀ (female)"]
  R1_2 = Resistor [tolerance=±5% resistance=1M package=THT]
  J1_2 = female pin header, 2 pins [form="♀ (female)"]
  J2_2 = female pin header, 2 pins [form="♀ (female)"]
  J3_2 = female pin header, 2 pins [form="♀ (female)"]

nets:
  N1: Raspberry_Pi1.GPIO0, R3.Pin_1, J1.pin2, J4.pin1
  N2: Raspberry_Pi1.GPIO2, R2.Pin_1, J1.pin3, J3.pin1
  N3: Raspberry_Pi1.GPIO3, R1.Pin_1, J1.pin4, J2.pin1
  N4: Raspberry_Pi1.Pin_9_DNC, R1.Pin_0, R2.Pin_0, R3.Pin_0, J1.pin1
  N5: Raspberry_Pi1.Pin_17_DNC, J1.pin5, J2.pin2, J3.pin2, J4.pin2
  N6: R2_2.Pin_0, J4_2.pin3, J2_2.pin2
  N7: R2_2.Pin_1, R3_2.Pin_1, J4_2.pin1, R1_2.Pin_1
  N8: R3_2.Pin_0, J4_2.pin4, J3_2.pin2
  N9: J4_2.pin2, R1_2.Pin_0, J1_2.pin2
  N10: J4_2.pin5, J1_2.pin1, J2_2.pin1, J3_2.pin1

notes:
  +3.3 a b c GND
